# Fritzing sketch Montage final (saved by Fritzing 0.9.3b)
breadboards: 2

parts:
  LED1 = LED - 5mm [color="Red (633nm)" package="5 mm [THT]"]
  LED2 = LED - 5mm [color="Red (633nm)" package="5 mm [THT]"]
  LED3 = LED - 5mm [color="Red (633nm)" package="5 mm [THT]"]
  LED4 = LED - 5mm [color="Red (633nm)" package="5 mm [THT]"]
  LED5 = LED - 5mm [color="Red (633nm)" package="5 mm [THT]"]
  LED7 = LED - 5mm [color="Red (633nm)" package="5 mm [THT]"]
  LED8 = LED - 5mm [color="Red (633nm)" package="5 mm [THT]"]
  LED9 = LED - 5mm [color="Red (633nm)" package="5 mm [THT]"]
  LED10 = LED - 5mm [color="Red (633nm)" package="5 mm [THT]"]
  Composant1 = Arduino Uno (Rev3)
  R2 = Resistor [tolerance=±5% resistance=220 package=THT]
  R3 = Resistor [tolerance=±5% resistance=220 package=THT]
  R4 = Resistor [tolerance=±5% resistance=220 package=THT]
  R5 = Resistor [tolerance=±5% resistance=220 package=THT]
  R6 = Resistor [tolerance=±5% resistance=220 package=THT]
  R7 = Resistor [tolerance=±5% resistance=220 package=THT]
  R8 = Resistor [tolerance=±5% resistance=220 package=THT]
  R9 = Resistor [tolerance=±5% resistance=220 package=THT]
  R10 = Resistor [tolerance=±5% resistance=220 package=THT]
  R1 = Resistor [tolerance=±5% resistance=220 package=THT]
  LED6 = LED - 5mm [color="Red (633nm)" package="5 mm [THT]"]
  U2 = LM124-324 Quad Opamp [package="DIP (Dual Inline)"]
  R11 = Resistor [tolerance=±5% resistance=470k package="2010 [SMD]"]
  R12 = Resistor [tolerance=±5% resistance=1k package="2010 [SMD]"]
  R13 = Resistor [tolerance=±5% resistance=68k package="2010 [SMD]"]
  R14 = Resistor [tolerance=±5% resistance=22k package="2010 [SMD]"]
  R16 = Resistor [tolerance=±5% resistance=100 package="2010 [SMD]"]
  C3 = Ceramic Capacitor [capacitance=1µF package="100 mil [THT, multilayer]"]
  C4 = Ceramic Capacitor [capacitance=100nF package="100 mil [THT, multilayer]"]
  R17 = PHOTOCELL [package=photocell]
  LED11 = LED - 5mm [color="Red (633nm)" package="5 mm [THT]"]
  R15 = Resistor [tolerance=±5% resistance=100 package="2010 [SMD]"]
  LED12 = LED - 5mm [color="Infrared (940nm)" package="5 mm [THT]"]

nets (from the breadboard view):
  N1: LED1.cathode, R1.Pin_0
  N2: LED1.anode, Composant1.D1/TX
  N3: LED2.cathode, R3.Pin_0
  N4: LED2.anode, Composant1.D2
  N5: LED3.cathode, R7.Pin_0
  N6: LED3.anode, Composant1.D4
  N7: LED4.cathode, R5.Pin_0
  N8: LED4.anode, Composant1.D3_PWM
  N9: LED5.cathode, R10.Pin_0
  N10: LED5.anode, Composant1.D5_PWM
  N11: LED7.cathode, R8.Pin_0
  N12: LED7.anode, Composant1.D6_PWM
  N13: LED8.cathode, R2.Pin_0
  N14: LED8.anode, Composant1.D10_PWM/SS
  N15: LED9.cathode, R4.Pin_0
  N16: LED9.anode, Composant1.D9_PWM
  N17: LED10.cathode, R6.Pin_0
  N18: LED10.anode, Composant1.D8
  N19: Composant1.A0, LED11.anode, R15.Pin_0
  N20: Composant1.GND, R2.Pin_1, R3.Pin_1, R4.Pin_1, R5.Pin_1, R6.Pin_1, R7.Pin_1, R8.Pin_1, R9.Pin_1, R10.Pin_1, R1.Pin_1, U2.VCC-, R12.Pin_1, R13.Pin_1, R16.Pin_0, R17.P$2, LED11.cathode
  N21: Composant1.D7, LED6.anode
  N22: Composant1.5V, U2.VCC+, R14.Pin_0, C3.1, LED12.anode
  N23: R9.Pin_0, LED6.cathode
  N24: U2.2IN+, R11.Pin_0, C4.0, R15.Pin_1
  N25: U2.2IN-, R11.Pin_1, R12.Pin_0, C4.1
  N26: U2.2OUT, R13.Pin_0, C3.0
  N27: R14.Pin_1, R17.P$1
  N28: R16.Pin_1, LED12.cathode
