# Fritzing sketch Montage module 1 (saved by Fritzing 0.9.3b)
breadboards: 1

parts:
  Composant1 = Arduino Uno (Rev3)
  R7 = PHOTOCELL [package=photocell]
  R5 = Resistor [tolerance=±5% resistance=1k package="2010 [SMD]"]
  R6 = Resistor [tolerance=±5% resistance=470k package="2010 [SMD]"]
  LED3 = LED - 5mm [color="Infrared (940nm)" package="5 mm [THT]"]
  R3 = Resistor [tolerance=±5% resistance=22k package="2010 [SMD]"]
  R2 = Resistor [tolerance=±5% resistance=100 package="2010 [SMD]"]
  R4 = Resistor [tolerance=±5% resistance=68k package="2010 [SMD]"]
  C1 = Ceramic Capacitor [capacitance=100nF package="100 mil [THT, multilayer]"]
  U1 = LM124-324 Quad Opamp [package="DIP (Dual Inline)"]
  R1 = Resistor [tolerance=±5% resistance=100 package="2010 [SMD]"]
  C2 = Ceramic Capacitor [capacitance=1µF package="100 mil [THT, multilayer]"]
  LED1 = LED - 5mm [color="Red (633nm)" package="5 mm [THT]"]

nets (from the schematic view):
  N1: Composant1.A0, R2.Pin_1, LED1.anode
  N2: Composant1.GND, R7.P$1, R5.Pin_0, LED3.cathode, R4.Pin_0, U1.VCC-, LED1.cathode
  N3: Composant1.5V, R3.Pin_1, U1.VCC+, R1.Pin_1
  N4: R7.P$2, R3.Pin_0, C2.1
  N5: R5.Pin_1, R6.Pin_0, C1.0, U1.2IN-
  N6: R6.Pin_1, R2.Pin_0, C1.1, U1.2OUT
  N7: LED3.anode, R1.Pin_0
  N8: R4.Pin_1, U1.2IN+, C2.0
